// Logisim project X64000.circ as structural Verilog: 4 circuits, main circuit ResetUnit
module ResetUnit (
  input  ResetIssue,
  output [15:0] ResetMagic
);

  and and_1 (ResetMagic[9], ResetIssue, 1'b1);
  not not_1 (ResetMagic[15], ResetMagic[9]);

  assign {ResetMagic[14:10], ResetMagic[8:0]} = {{7{ResetMagic[15]}}, ResetMagic[9], ResetMagic[15], ResetMagic[9], ResetMagic[15], ResetMagic[9], ResetMagic[15], ResetMagic[9]};

  // Other names for the same wires on the sheet: RST[15:0] = {{6{ResetMagic[15]}}, ResetMagic[9], {2{ResetMagic[15]}}, ResetMagic[9], ResetMagic[15], ResetMagic[9], ResetMagic[15], ResetMagic[9], ResetMagic[15], ResetMagic[9]}

  // Notes on the sheet:
  //   32k reset line
endmodule

module RegisterUnit (
  input  [63:0] RegisterValue,
  input  [7:0] RegisterIndex,
  input  RegAccept,
  output [7:0] RegisterIndexValue,
  output [63:0] RegisterOutputValue
);

  wire Clk_out, RegEnable, RegWrite, undriven, undriven_2, xor_1_out, xor_2_out, xor_3_out, xor_4_out,
       xor_5_out, xor_6_out;

  and and_1 (RegWrite, RegEnable, RegAccept);
  Register #(.width(64)) register_1 (
    .D(RegisterValue), .en(RegWrite), .clk(Clk_out), .Q(RegisterOutputValue), .clr(undriven));
  // NoConnect on undriven
  xor xor_1 (xor_1_out, RegisterIndex[0], RegisterIndex[1]);
  xor xor_2 (xor_2_out, RegisterIndex[2], RegisterIndex[3]);
  xor xor_3 (xor_3_out, RegisterIndex[4], RegisterIndex[5]);
  xor xor_4 (xor_4_out, RegisterIndex[6], RegisterIndex[7]);
  Clock Clk (.out(Clk_out));
  xor xor_5 (xor_5_out, xor_1_out, xor_2_out);
  xor xor_6 (xor_6_out, xor_3_out, xor_4_out);
  Register IndexRegister (.D(RegisterIndex), .en(RegWrite), .clk(Clk_out), .Q(RegisterIndexValue), .clr(undriven_2));
  // NoConnect on undriven_2
  xor xor_7 (RegEnable, xor_5_out, xor_6_out);

  // Other names for the same wires on the sheet: RegisterValueTunnel[63:0] = RegisterValue

  // Notes on the sheet:
  //   32k register file
  //   we get the index and put inside
  //   this register
  //   This is like an array
endmodule

module Register64 (
  input  [63:0] InValue,
  input  [7:0] Magic,
  input  IsAddress
);

  wire and_2_out, and_3_out, not_1_out, not_2_out, R2Accept;
  wire [7:0] R2Index;
  wire [63:0] R2Value;

  and and_1 (R2Accept, and_2_out, and_3_out);
  and and_2 (and_2_out, 1'b1, Magic[1]);
  and and_3 (and_3_out, not_2_out, not_1_out);
  not not_1 (not_1_out, 1'b0);
  not not_2 (not_2_out, Magic[0]);
  RegisterUnit RegUni (
    .RegisterValue(InValue), .RegisterIndex(8'h2), .RegAccept(R2Accept), .RegisterIndexValue(R2Index),
    .RegisterOutputValue(R2Value));

  // Other names for the same wires on the sheet: Line[7:0] = Magic; R2ValueIn[63:0] = InValue;
  //   ValueIn[63:0] = InValue

  // Notes on the sheet:
  //   Register input
endmodule

module X1001 (
  input  LA,
  input  LB,
  input  SRC,
  input  in_4,
  input  in_5,
  input  in_6,
  input  in_7,
  output DRAIN,
  output out_9,
  output out_10
);

  wire not_1_out, not_2_out, not_3_out, pull_resistor_3_node;

  Pull_Resistor pull_resistor_1 (.node(out_10));
  Pull_Resistor pull_resistor_2 (.node(DRAIN));
  not not_1 (not_1_out, LA);
  Pull_Resistor pull_resistor_3 (.node(pull_resistor_3_node));
  not not_2 (not_2_out, LB);
  not not_3 (not_3_out, in_5);
  Transistor transistor_1 (.in(in_7), .out(out_10), .gate(not_3_out));
  Transistor transistor_2 (.in(pull_resistor_3_node), .out(DRAIN), .gate(not_1_out));
  Transistor transistor_3 (.in(SRC), .out(pull_resistor_3_node), .gate(not_2_out));
  Pull_Resistor pull_resistor_4 (.node(out_9));
  Transistor transistor_4 (.in(in_6), .out(out_9), .gate(in_4));
endmodule
